// Logisim project y86-64.circ as structural Verilog
module main (
  output [15:0] NewPC
);

  wire and_1_out, clock_1_out, decoder_1_out10, decoder_1_out11, decoder_1_out12, decoder_1_out13,
       execute_1_outcond, not_1_out, or_1_out, pla_1_out;
  wire [1:0] dstAorE_out, dstBorM_out, srcA_out, srcB_out;
  wire [3:0] adder_1_out, instructionmemory_1_icode, instructionmemory_1_ifun, instructionmemory_1_ra,
       instructionmemory_1_rb, multiplexer_2_out, multiplexer_3_out, multiplexer_4_out, multiplexer_5_out,
       register_1_q;
  wire [7:0] ram_1_dout;
  wire [15:0] adder_2_out, adder_3_out, PC_Increment_out, PC_q, valE_q;
  wire [47:0] valE_q_2;
  wire [63:0] execute_1_outvalc, instructionmemory_1_valc, registerfile_1_vala, registerfile_1_valb, valM_q;

  Clock clock_1 (.out(clock_1_out));
  Register #(.width(16)) PC (.D(NewPC), .en(decoder_1_out13), .clk(decoder_1_out13), .Q(PC_q));  // open: clr
  Register #(.width(4)) register_1 (
    .D(adder_1_out), .en(1'b1), .clk(clock_1_out), .Q(register_1_q), .clr(decoder_1_out13));
  Adder #(.width(4)) adder_1 (.a(register_1_q), .b(4'b0001), .out(adder_1_out));  // open: cin, cout
  Adder #(.width(16)) adder_2 (.a(PC_q), .b({{12{1'b0}}, register_1_q}), .out(adder_2_out));  // open: cin, cout
  RAM #(.addrWidth(16), .asyncread("true"), .\type ("nonvolatile")) ram_1 (
    .addr(adder_2_out), .we(1'b0), .oe(1'b1), .clk(clock_1_out), .dout(ram_1_dout));  // open: din
  Decoder #(.select(4)) decoder_1 (
    .out10(decoder_1_out10), .out11(decoder_1_out11), .out12(decoder_1_out12), .out13(decoder_1_out13),
    .sel(register_1_q), .en(clock_1_out));  // open: out0, out1, out2, out3, out4, out5, out6, out7, out8, out9, out14, out15
  PLA #(.in_width(4), .out_width(16), .\table ("0000 0000000000000000 # halt 0\n0001 0000000000000001 # nop 1\n0010 0000000000000010 # rrmovq 2\n0011 0000000000001010 # irmovq 10\n0100 0000000000001010 # mrmovq 10\n0101 0000000000001010 # rmmovq 10\n0110 0000000000000010 # OPq 2\n0111 0000000000001001 # jXX 9\n1000 0000000000001001 # call 9\n1001 0000000000000001 # ret 1\n1010 0000000000000010 # pushq 2\n1011 0000000000000010 # popq 2\nxxxx 0000000000000000 # invalid instruction")) PC_Increment (
    .in(instructionmemory_1_icode), .out(PC_Increment_out));
  InstructionMemory instructionmemory_1 (
    .Data(ram_1_dout), .Clk(clock_1_out), .Position(register_1_q), .icode(instructionmemory_1_icode),
    .ifun(instructionmemory_1_ifun), .rA(instructionmemory_1_ra), .rB(instructionmemory_1_rb),
    .valC(instructionmemory_1_valc));
  Multiplexer #(.width(16)) multiplexer_1 (.in0(adder_3_out), .in1(valE_q), .out(NewPC), .sel(and_1_out));
  Adder #(.width(16)) adder_3 (.a(PC_Increment_out), .b(PC_q), .out(adder_3_out));  // open: cin, cout
  PLA #(.in_width(4), .\table ("0000 00 # halt F\n0001 00 # nop F\n0010 10 # rrmovq rB\n0011 10 # irmovq rB\n0100 01 # mrmovq rA\n0101 00 # rmmovq F\n0110 10 # OPq rB\n0111 00 # jXX F\n1000 11 # call RSP\n1001 11 # ret RSP\n1010 11 # pushq RSP\n1011 11 # popq RSP\nxxxx 00 # invalid instruction")) dstAorE (
    .in(instructionmemory_1_icode), .out(dstAorE_out));
  PLA #(.in_width(4), .\table ("0000 00 # halt F\n0001 00 # nop F\n0010 00 # rrmovq F\n0011 00 # irmovq F\n0100 01 # mrmovq rA\n0101 00 # rmmovq F\n0110 00 # OPq F\n0111 00 # jXX F\n1000 00 # call F\n1001 00 # ret F\n1010 11 # pushq RSP\n1011 01 # popq rA\nxxxx 00 # invalid instruction")) dstBorM (
    .in(instructionmemory_1_icode), .out(dstBorM_out));
  Register #(.width(64)) valM (.D(64'h10), .en(clock_1_out), .clk(clock_1_out), .Q(valM_q));  // open: clr
  PLA #(.in_width(4), .\table ("0000 00 # halt F\n0001 00 # nop F\n0010 01 # rrmovq rA\n0011 00 # irmovq F\n0100 01 # mrmovq rA\n0101 01 # rmmovq rA\n0110 01 # OPq rA\n0111 00 # jXX F\n1000 00 # call F\n1001 00 # ret F\n1010 01 # pushq RSP\n1011 10 # popq rA\nxxxx 00 # invalid instruction")) srcA (
    .in(instructionmemory_1_icode), .out(srcA_out));
  PLA #(.in_width(4), .\table ("0000 00 # halt F\n0001 00 # nop F\n0010 01 # rrmovq rB\n0011 00 # irmovq F\n0100 01 # mrmovq rB\n0101 01 # rmmovq rB\n0110 01 # OPq rB\n0111 00 # jXX F\n1000 00 # call F\n1001 00 # ret F\n1010 10 # pushq RSP\n1011 10 # popq RSP\nxxxx 00 # invalid instruction")) srcB (
    .in(instructionmemory_1_icode), .out(srcB_out));
  and and_1 (and_1_out, execute_1_outcond, pla_1_out);
  PLA #(.in_width(4), .out_width(1), .\table ("0111 1 # jmp\nxxxx 0 # not jmp")) pla_1 (
    .in(instructionmemory_1_icode), .out(pla_1_out));
  Multiplexer #(.select(2), .width(4)) multiplexer_2 (
    .in0(4'b1111), .in1(instructionmemory_1_ra), .in2(instructionmemory_1_rb), .in3(4'b0100),
    .out(multiplexer_2_out), .sel(dstAorE_out));
  Multiplexer #(.select(2), .width(4)) multiplexer_3 (
    .in0(4'b1111), .in1(instructionmemory_1_ra), .in2(instructionmemory_1_rb), .in3(4'b0100),
    .out(multiplexer_3_out), .sel(dstBorM_out));
  Multiplexer #(.select(2), .width(4)) multiplexer_4 (
    .in0(4'b1111), .in1(instructionmemory_1_ra), .in2(4'b0100), .out(multiplexer_4_out), .sel(srcA_out));  // open: in3
  Multiplexer #(.select(2), .width(4)) multiplexer_5 (
    .in0(4'b1111), .in1(instructionmemory_1_rb), .in2(4'b0100), .out(multiplexer_5_out), .sel(srcB_out));  // open: in3
  not not_1 (not_1_out, decoder_1_out12);
  or or_1 (or_1_out, decoder_1_out12, decoder_1_out10);
  RegisterFile registerfile_1 (
    .dataA({valE_q_2, valE_q}), .dataB(valM_q), .dstA(multiplexer_2_out), .dstB(multiplexer_3_out),
    .write_enable(decoder_1_out12), .read_enable(not_1_out), .clk(or_1_out), .srcA(multiplexer_4_out),
    .srcB(multiplexer_5_out), .valA(registerfile_1_vala), .valB(registerfile_1_valb));
  Execute execute_1 (
    .icode(instructionmemory_1_icode), .ifun(instructionmemory_1_ifun), .valC(instructionmemory_1_valc),
    .valA(registerfile_1_vala), .valB(registerfile_1_valb), .clk(decoder_1_out11),
    .outValC(execute_1_outvalc), .outCond(execute_1_outcond));
  Register #(.width(64)) valE (
    .D(execute_1_outvalc), .en(decoder_1_out11), .clk(decoder_1_out11), .Q({valE_q_2, valE_q}));  // open: clr
endmodule

module InstructionMemory (
  input  [7:0] Data,
  input  Clk,
  input  [3:0] Position,
  output [3:0] icode,
  output [3:0] ifun,
  output [3:0] rA,
  output [3:0] rB,
  output [63:0] valC
);

  wire decoder_1_out0, decoder_1_out1, decoder_1_out2, decoder_1_out3, decoder_1_out4, decoder_1_out5,
       decoder_1_out6, decoder_1_out7, decoder_1_out8, decoder_1_out9, NotJumpOrCall_out;
  wire [7:0] register_7_q, register_8_q, register_9_q, register_10_q;
  wire [39:0] register_2_q;

  Register register_1 (.D(Data), .en(decoder_1_out0), .clk(Clk), .Q({icode, ifun}));  // open: clr
  Decoder #(.enable("false"), .select(4)) decoder_1 (
    .out0(decoder_1_out0), .out1(decoder_1_out1), .out2(decoder_1_out2), .out3(decoder_1_out3),
    .out4(decoder_1_out4), .out5(decoder_1_out5), .out6(decoder_1_out6), .out7(decoder_1_out7),
    .out8(decoder_1_out8), .out9(decoder_1_out9), .sel(Position));  // open: out10, out11, out12, out13, out14, out15
  Register register_2 (.D(Data), .en(decoder_1_out1), .clk(Clk), .Q(register_2_q[7:0]));  // open: clr
  Register register_3 (.D(Data), .en(decoder_1_out2), .clk(Clk), .Q(register_2_q[15:8]));  // open: clr
  PLA #(.in_width(4), .out_width(1), .\table ("0111 0 # 7 jmp\n1000 0 # 8 call\nxxxx 1")) NotJumpOrCall (
    .in(icode), .out(NotJumpOrCall_out));
  Multiplexer #(.width(8)) multiplexer_1 (
    .in0({8{1'b1}}), .in1(register_2_q[7:0]), .out({rA, rB}), .sel(NotJumpOrCall_out));
  Register register_4 (.D(Data), .en(decoder_1_out3), .clk(Clk), .Q(register_2_q[23:16]));  // open: clr
  Register register_5 (.D(Data), .en(decoder_1_out4), .clk(Clk), .Q(register_2_q[31:24]));  // open: clr
  Register register_6 (.D(Data), .en(decoder_1_out5), .clk(Clk), .Q(register_2_q[39:32]));  // open: clr
  Register register_7 (.D(Data), .en(decoder_1_out6), .clk(Clk), .Q(register_7_q));  // open: clr
  Register register_8 (.D(Data), .en(decoder_1_out7), .clk(Clk), .Q(register_8_q));  // open: clr
  Register register_9 (.D(Data), .en(decoder_1_out8), .clk(Clk), .Q(register_9_q));  // open: clr
  Register register_10 (.D(Data), .en(decoder_1_out9), .clk(Clk), .Q(register_10_q));  // open: clr
  Multiplexer #(.width(64)) multiplexer_2 (
    .in0({register_9_q, register_8_q, register_7_q, register_2_q}),
    .in1({register_10_q, register_9_q, register_8_q, register_7_q, register_2_q[39:8]}), .out(valC),
    .sel(NotJumpOrCall_out));
endmodule

module RegisterFile (
  input  [63:0] dataA,
  input  [63:0] dataB,
  input  [3:0] dstA,
  input  [3:0] dstB,
  input  write_enable,
  input  read_enable,
  input  clk,
  input  [3:0] srcA,
  input  [3:0] srcB,
  output [63:0] valA,
  output [63:0] valB
);

  wire and_1_out, decoder_1_out0, decoder_1_out1, decoder_1_out2, decoder_1_out3, decoder_1_out4,
       decoder_1_out5, decoder_1_out6, decoder_1_out7, decoder_1_out8, decoder_1_out9, decoder_1_out10,
       decoder_1_out11, decoder_1_out12, decoder_1_out13, decoder_1_out14, decoder_2_out0, decoder_2_out1,
       decoder_2_out2, decoder_2_out3, decoder_2_out4, decoder_2_out5, decoder_2_out6, decoder_2_out7,
       decoder_2_out8, decoder_2_out9, decoder_2_out10, decoder_2_out11, decoder_2_out12, decoder_2_out13,
       decoder_2_out14, decoder_3_out0, decoder_3_out1, decoder_3_out2, decoder_3_out3, decoder_3_out4,
       decoder_3_out5, decoder_3_out6, decoder_3_out7, decoder_3_out8, decoder_3_out9, decoder_3_out10,
       decoder_3_out11, decoder_3_out12, decoder_3_out13, decoder_3_out14, decoder_3_out15, decoder_4_out0,
       decoder_4_out1, decoder_4_out2, decoder_4_out3, decoder_4_out4, decoder_4_out5, decoder_4_out6,
       decoder_4_out7, decoder_4_out8, decoder_4_out9, decoder_4_out10, decoder_4_out11, decoder_4_out12,
       decoder_4_out13, decoder_4_out14, decoder_4_out15, xor_1_out, xor_2_out, xor_3_out, xor_4_out,
       xor_5_out, xor_6_out, xor_7_out, xor_8_out, xor_9_out, xor_10_out, xor_11_out, xor_12_out, xor_13_out,
       xor_14_out, xor_15_out;
  wire [63:0] controlled_buffer_1_out, controlled_buffer_6_out, controlled_buffer_10_out,
       controlled_buffer_14_out, controlled_buffer_18_out, controlled_buffer_22_out,
       controlled_buffer_26_out, controlled_buffer_30_out, controlled_buffer_34_out,
       controlled_buffer_38_out, controlled_buffer_42_out, controlled_buffer_46_out,
       controlled_buffer_51_out, controlled_buffer_54_out, controlled_buffer_59_out, R8_q, R9_q, R10_q,
       R11_q, R12_q, R13_q, R14_q, RAX_q, RBP_q, RBX_q, RCX_q, RDI_q, RDX_q, RSI_q, RSP_q;

  Decoder #(.select(4)) decoder_1 (
    .out0(decoder_1_out0), .out1(decoder_1_out1), .out2(decoder_1_out2), .out3(decoder_1_out3),
    .out4(decoder_1_out4), .out5(decoder_1_out5), .out6(decoder_1_out6), .out7(decoder_1_out7),
    .out8(decoder_1_out8), .out9(decoder_1_out9), .out10(decoder_1_out10), .out11(decoder_1_out11),
    .out12(decoder_1_out12), .out13(decoder_1_out13), .out14(decoder_1_out14), .sel(dstA), .en(and_1_out));  // open: out15
  Decoder #(.select(4)) decoder_2 (
    .out0(decoder_2_out0), .out1(decoder_2_out1), .out2(decoder_2_out2), .out3(decoder_2_out3),
    .out4(decoder_2_out4), .out5(decoder_2_out5), .out6(decoder_2_out6), .out7(decoder_2_out7),
    .out8(decoder_2_out8), .out9(decoder_2_out9), .out10(decoder_2_out10), .out11(decoder_2_out11),
    .out12(decoder_2_out12), .out13(decoder_2_out13), .out14(decoder_2_out14), .sel(dstB), .en(and_1_out));  // open: out15
  and and_1 (and_1_out, write_enable, clk);
  Decoder #(.select(4)) decoder_3 (
    .out0(decoder_3_out0), .out1(decoder_3_out1), .out2(decoder_3_out2), .out3(decoder_3_out3),
    .out4(decoder_3_out4), .out5(decoder_3_out5), .out6(decoder_3_out6), .out7(decoder_3_out7),
    .out8(decoder_3_out8), .out9(decoder_3_out9), .out10(decoder_3_out10), .out11(decoder_3_out11),
    .out12(decoder_3_out12), .out13(decoder_3_out13), .out14(decoder_3_out14), .out15(decoder_3_out15),
    .sel(srcA), .en(read_enable));
  Decoder #(.select(4)) decoder_4 (
    .out0(decoder_4_out0), .out1(decoder_4_out1), .out2(decoder_4_out2), .out3(decoder_4_out3),
    .out4(decoder_4_out4), .out5(decoder_4_out5), .out6(decoder_4_out6), .out7(decoder_4_out7),
    .out8(decoder_4_out8), .out9(decoder_4_out9), .out10(decoder_4_out10), .out11(decoder_4_out11),
    .out12(decoder_4_out12), .out13(decoder_4_out13), .out14(decoder_4_out14), .out15(decoder_4_out15),
    .sel(srcB), .en(read_enable));
  xor xor_1 (xor_1_out, decoder_1_out0, decoder_2_out0);
  assign controlled_buffer_1_out = decoder_1_out0 ? dataA : 64'bz;  // Controlled_Buffer controlled_buffer_1
  assign controlled_buffer_1_out = decoder_2_out0 ? dataB : 64'bz;  // Controlled_Buffer controlled_buffer_2
  Register #(.width(64)) RAX (.D(controlled_buffer_1_out), .en(xor_1_out), .clk(xor_1_out), .Q(RAX_q));  // open: clr
  assign valA = decoder_3_out15 ? {64{1'b0}} : 64'bz;  // Controlled_Buffer controlled_buffer_3
  assign valB = decoder_4_out15 ? {64{1'b0}} : 64'bz;  // Controlled_Buffer controlled_buffer_4
  xor xor_2 (xor_2_out, decoder_1_out1, decoder_2_out1);
  assign valA = decoder_3_out0 ? RAX_q : 64'bz;  // Controlled_Buffer controlled_buffer_5
  assign controlled_buffer_6_out = decoder_1_out1 ? dataA : 64'bz;  // Controlled_Buffer controlled_buffer_6
  assign controlled_buffer_6_out = decoder_2_out1 ? dataB : 64'bz;  // Controlled_Buffer controlled_buffer_7
  Register #(.width(64)) RCX (.D(controlled_buffer_6_out), .en(xor_2_out), .clk(xor_2_out), .Q(RCX_q));  // open: clr
  assign valB = decoder_4_out0 ? RAX_q : 64'bz;  // Controlled_Buffer controlled_buffer_8
  xor xor_3 (xor_3_out, decoder_1_out2, decoder_2_out2);
  assign valA = decoder_3_out1 ? RCX_q : 64'bz;  // Controlled_Buffer controlled_buffer_9
  assign controlled_buffer_10_out = decoder_1_out2 ? dataA : 64'bz;  // Controlled_Buffer controlled_buffer_10
  assign controlled_buffer_10_out = decoder_2_out2 ? dataB : 64'bz;  // Controlled_Buffer controlled_buffer_11
  Register #(.width(64)) RDX (.D(controlled_buffer_10_out), .en(xor_3_out), .clk(xor_3_out), .Q(RDX_q));  // open: clr
  assign valB = decoder_4_out1 ? RCX_q : 64'bz;  // Controlled_Buffer controlled_buffer_12
  xor xor_4 (xor_4_out, decoder_1_out3, decoder_2_out3);
  assign valA = decoder_3_out2 ? RDX_q : 64'bz;  // Controlled_Buffer controlled_buffer_13
  assign controlled_buffer_14_out = decoder_1_out3 ? dataA : 64'bz;  // Controlled_Buffer controlled_buffer_14
  assign controlled_buffer_14_out = decoder_2_out3 ? dataB : 64'bz;  // Controlled_Buffer controlled_buffer_15
  Register #(.width(64)) RBX (.D(controlled_buffer_14_out), .en(xor_4_out), .clk(xor_4_out), .Q(RBX_q));  // open: clr
  assign valB = decoder_4_out2 ? RDX_q : 64'bz;  // Controlled_Buffer controlled_buffer_16
  assign valA = decoder_3_out3 ? RBX_q : 64'bz;  // Controlled_Buffer controlled_buffer_17
  xor xor_5 (xor_5_out, decoder_1_out4, decoder_2_out4);
  assign controlled_buffer_18_out = decoder_1_out4 ? dataA : 64'bz;  // Controlled_Buffer controlled_buffer_18
  assign controlled_buffer_18_out = decoder_2_out4 ? dataB : 64'bz;  // Controlled_Buffer controlled_buffer_19
  Register #(.width(64)) RSP (.D(controlled_buffer_18_out), .en(xor_5_out), .clk(xor_5_out), .Q(RSP_q));  // open: clr
  assign valB = decoder_4_out3 ? RBX_q : 64'bz;  // Controlled_Buffer controlled_buffer_20
  assign valA = decoder_3_out4 ? RSP_q : 64'bz;  // Controlled_Buffer controlled_buffer_21
  xor xor_6 (xor_6_out, decoder_1_out5, decoder_2_out5);
  assign controlled_buffer_22_out = decoder_1_out5 ? dataA : 64'bz;  // Controlled_Buffer controlled_buffer_22
  assign controlled_buffer_22_out = decoder_2_out5 ? dataB : 64'bz;  // Controlled_Buffer controlled_buffer_23
  Register #(.width(64)) RBP (.D(controlled_buffer_22_out), .en(xor_6_out), .clk(xor_6_out), .Q(RBP_q));  // open: clr
  assign valB = decoder_4_out4 ? RSP_q : 64'bz;  // Controlled_Buffer controlled_buffer_24
  assign valA = decoder_3_out5 ? RBP_q : 64'bz;  // Controlled_Buffer controlled_buffer_25
  xor xor_7 (xor_7_out, decoder_1_out6, decoder_2_out6);
  assign controlled_buffer_26_out = decoder_1_out6 ? dataA : 64'bz;  // Controlled_Buffer controlled_buffer_26
  assign controlled_buffer_26_out = decoder_2_out6 ? dataB : 64'bz;  // Controlled_Buffer controlled_buffer_27
  Register #(.width(64)) RSI (.D(controlled_buffer_26_out), .en(xor_7_out), .clk(xor_7_out), .Q(RSI_q));  // open: clr
  assign valB = decoder_4_out5 ? RBP_q : 64'bz;  // Controlled_Buffer controlled_buffer_28
  assign valA = decoder_3_out6 ? RSI_q : 64'bz;  // Controlled_Buffer controlled_buffer_29
  xor xor_8 (xor_8_out, decoder_1_out7, decoder_2_out7);
  assign controlled_buffer_30_out = decoder_1_out7 ? dataA : 64'bz;  // Controlled_Buffer controlled_buffer_30
  assign controlled_buffer_30_out = decoder_2_out7 ? dataB : 64'bz;  // Controlled_Buffer controlled_buffer_31
  Register #(.width(64)) RDI (.D(controlled_buffer_30_out), .en(xor_8_out), .clk(xor_8_out), .Q(RDI_q));  // open: clr
  assign valB = decoder_4_out6 ? RSI_q : 64'bz;  // Controlled_Buffer controlled_buffer_32
  assign valA = decoder_3_out7 ? RDI_q : 64'bz;  // Controlled_Buffer controlled_buffer_33
  xor xor_9 (xor_9_out, decoder_1_out8, decoder_2_out8);
  assign controlled_buffer_34_out = decoder_1_out8 ? dataA : 64'bz;  // Controlled_Buffer controlled_buffer_34
  assign controlled_buffer_34_out = decoder_2_out8 ? dataB : 64'bz;  // Controlled_Buffer controlled_buffer_35
  Register #(.width(64)) R8 (.D(controlled_buffer_34_out), .en(xor_9_out), .clk(xor_9_out), .Q(R8_q));  // open: clr
  assign valB = decoder_4_out7 ? RDI_q : 64'bz;  // Controlled_Buffer controlled_buffer_36
  assign valA = decoder_3_out8 ? R8_q : 64'bz;  // Controlled_Buffer controlled_buffer_37
  xor xor_10 (xor_10_out, decoder_1_out9, decoder_2_out9);
  assign controlled_buffer_38_out = decoder_1_out9 ? dataA : 64'bz;  // Controlled_Buffer controlled_buffer_38
  assign controlled_buffer_38_out = decoder_2_out9 ? dataB : 64'bz;  // Controlled_Buffer controlled_buffer_39
  Register #(.width(64)) R9 (.D(controlled_buffer_38_out), .en(xor_10_out), .clk(xor_10_out), .Q(R9_q));  // open: clr
  assign valB = decoder_4_out8 ? R8_q : 64'bz;  // Controlled_Buffer controlled_buffer_40
  assign valA = decoder_3_out9 ? R9_q : 64'bz;  // Controlled_Buffer controlled_buffer_41
  xor xor_11 (xor_11_out, decoder_1_out10, decoder_2_out10);
  assign controlled_buffer_42_out = decoder_1_out10 ? dataA : 64'bz;  // Controlled_Buffer controlled_buffer_42
  assign controlled_buffer_42_out = decoder_2_out10 ? dataB : 64'bz;  // Controlled_Buffer controlled_buffer_43
  Register #(.width(64)) R10 (.D(controlled_buffer_42_out), .en(xor_11_out), .clk(xor_11_out), .Q(R10_q));  // open: clr
  assign valB = decoder_4_out9 ? R9_q : 64'bz;  // Controlled_Buffer controlled_buffer_44
  assign valA = decoder_3_out10 ? R10_q : 64'bz;  // Controlled_Buffer controlled_buffer_45
  xor xor_12 (xor_12_out, decoder_1_out11, decoder_2_out11);
  assign controlled_buffer_46_out = decoder_1_out11 ? dataA : 64'bz;  // Controlled_Buffer controlled_buffer_46
  assign valB = decoder_4_out10 ? R10_q : 64'bz;  // Controlled_Buffer controlled_buffer_47
  assign controlled_buffer_46_out = decoder_2_out11 ? dataB : 64'bz;  // Controlled_Buffer controlled_buffer_48
  Register #(.width(64)) R11 (.D(controlled_buffer_46_out), .en(xor_12_out), .clk(xor_12_out), .Q(R11_q));  // open: clr
  xor xor_13 (xor_13_out, decoder_1_out12, decoder_2_out12);
  assign valA = decoder_3_out11 ? R11_q : 64'bz;  // Controlled_Buffer controlled_buffer_49
  assign valB = decoder_4_out11 ? R11_q : 64'bz;  // Controlled_Buffer controlled_buffer_50
  assign controlled_buffer_51_out = decoder_1_out12 ? dataA : 64'bz;  // Controlled_Buffer controlled_buffer_51
  assign controlled_buffer_51_out = decoder_2_out12 ? dataB : 64'bz;  // Controlled_Buffer controlled_buffer_52
  Register #(.width(64)) R12 (.D(controlled_buffer_51_out), .en(xor_13_out), .clk(xor_13_out), .Q(R12_q));  // open: clr
  assign valA = decoder_3_out12 ? R12_q : 64'bz;  // Controlled_Buffer controlled_buffer_53
  xor xor_14 (xor_14_out, decoder_1_out13, decoder_2_out13);
  assign controlled_buffer_54_out = decoder_1_out13 ? dataA : 64'bz;  // Controlled_Buffer controlled_buffer_54
  assign controlled_buffer_54_out = decoder_2_out13 ? dataB : 64'bz;  // Controlled_Buffer controlled_buffer_55
  Register #(.width(64)) R13 (.D(controlled_buffer_54_out), .en(xor_14_out), .clk(xor_14_out), .Q(R13_q));  // open: clr
  assign valB = decoder_4_out12 ? R12_q : 64'bz;  // Controlled_Buffer controlled_buffer_56
  assign valA = decoder_3_out13 ? R13_q : 64'bz;  // Controlled_Buffer controlled_buffer_57
  xor xor_15 (xor_15_out, decoder_1_out14, decoder_2_out14);
  assign valB = decoder_4_out13 ? R13_q : 64'bz;  // Controlled_Buffer controlled_buffer_58
  assign controlled_buffer_59_out = decoder_1_out14 ? dataA : 64'bz;  // Controlled_Buffer controlled_buffer_59
  assign controlled_buffer_59_out = decoder_2_out14 ? dataB : 64'bz;  // Controlled_Buffer controlled_buffer_60
  Register #(.width(64)) R14 (.D(controlled_buffer_59_out), .en(xor_15_out), .clk(xor_15_out), .Q(R14_q));  // open: clr
  assign valA = decoder_3_out14 ? R14_q : 64'bz;  // Controlled_Buffer controlled_buffer_61
  assign valB = decoder_4_out14 ? R14_q : 64'bz;  // Controlled_Buffer controlled_buffer_62
endmodule

module Execute (
  input  [3:0] icode,
  input  [3:0] ifun,
  input  [63:0] valC,
  input  [63:0] valA,
  input  [63:0] valB,
  input  clk,
  output [63:0] outValC,
  output outCond
);

  wire alu_1_overflow, alu_1_sf, alu_1_zf, aluB_out, and_1_out, OvrF_q, setCC_out, SF_q, ZF_q;
  wire [1:0] ALUfun_out;
  wire [2:0] aluA_out;
  wire [63:0] multiplexer_1_out, multiplexer_2_out;

  PLA #(.in_width(8), .\table ("01100000 10 # addq\n01100001 11 # subq\n01100010 00 # andq\n01100011 01 # xorq\nxxxxxxxx 10 # jmp")) ALUfun (
    .in({icode, ifun}), .out(ALUfun_out));
  PLA #(.in_width(4), .out_width(3), .\table ("0010 000 # cmovXX - valA\n0011 010 # irmovq - valC\n0100 000 # rmmovq - valA\n0101 001 # mrmovq - valB\n0110 000 # OPq - valA\n1000 100 # call - -8\n1001 011 # ret - +8\n1010 100 # pushq - -8\n1011 011 # popq - +8\n0111 010 # jxx - valC")) aluA (
    .in(icode), .out(aluA_out));
  Multiplexer #(.select(3), .width(64)) multiplexer_1 (
    .in0(valA), .in1(valB), .in2(valC), .in3(64'h8), .in4(64'hfffffffffffffff8), .out(multiplexer_1_out),
    .sel(aluA_out));  // open: in5, in6, in7
  PLA #(.in_width(4), .out_width(1), .\table ("0010 0 # cmovXX - 0\n0011 0 # irmovq - 0\n0100 1 # rmmovq - valB\n0101 1 # mrmovq - valB\n0110 1 # OPq - valB\n1000 1 # call - valB\n1001 1 # ret - valB\n1010 1 # pushq - valB\n1011 1 # popq - valB")) aluB (
    .in(icode), .out(aluB_out));
  Multiplexer #(.width(64)) multiplexer_2 (.in0({64{1'b0}}), .in1(valB), .out(multiplexer_2_out), .sel(aluB_out));
  PLA #(.in_width(4), .out_width(1), .\table ("0110 1 # opq - all flags\n0010 1 # cmov")) setCC (
    .in(icode), .out(setCC_out));
  ALU alu_1 (
    .aluA(multiplexer_1_out), .aluB(multiplexer_2_out), .ALUfun(ALUfun_out), .Overflow(alu_1_overflow),
    .SF(alu_1_sf), .valE(outValC), .ZF(alu_1_zf));
  and and_1 (and_1_out, setCC_out, clk);
  D_Flip_Flop OvrF (.D(alu_1_overflow), .clk(and_1_out), .Q(OvrF_q));  // open: Qn, preset, reset
  D_Flip_Flop SF (.D(alu_1_sf), .clk(and_1_out), .Q(SF_q));  // open: Qn, preset, reset
  D_Flip_Flop ZF (.D(alu_1_zf), .clk(and_1_out), .Q(ZF_q));  // open: Qn, preset, reset
  condition condition_1 (.zeroflag(ZF_q), .signflag(SF_q), .overflow(OvrF_q), .ifun(ifun), .out_5(outCond));

  // Notes on the sheet:
  //   valA = 0 | valB= 1 | valC = 2 | 8 = 3 | -8 = 4
  //   ALUfun: 00 = AND | 01 = NOR | 10 = + | 11 = -
  //   0 = 0 | valB = 1
  //   (zero f/Sign f/Overflow f) 
endmodule

module ALU (
  input  [63:0] aluA,
  input  [63:0] aluB,
  input  [1:0] ALUfun,
  output Overflow,
  output SF,
  output [63:0] valE,
  output ZF
);

  wire adder_1_cout, and_2_out, comparator_2_lt, comparator_3_lt, comparator_4_lt, xnor_1_out, xor_2_out;
  wire [63:0] adder_1_out, and_1_out, subtractor_1_out, xor_1_out;

  assign and_1_out = aluA & aluB;  // AND_Gate and_1, 64 bits wide
  assign xor_1_out = aluA ^ aluB;  // XOR_Gate xor_1, 64 bits wide
  Adder #(.width(64)) adder_1 (.a(aluB), .b(aluA), .out(adder_1_out), .cin(1'b0), .cout(adder_1_cout));
  Subtractor #(.width(64)) subtractor_1 (.a(aluB), .b(aluA), .out(subtractor_1_out), .bin(1'b0), .bout(SF));
  Multiplexer #(.select(2), .width(64)) multiplexer_1 (
    .in0(and_1_out), .in1(xor_1_out), .in2(adder_1_out), .in3(subtractor_1_out), .out(valE), .sel(ALUfun));
  Comparator #(.width(64)) comparator_1 (.a(valE), .b({64{1'b0}}), .eq(ZF));  // open: gt, lt
  Comparator #(.width(64)) comparator_2 (.a(aluA), .b({64{1'b0}}), .lt(comparator_2_lt));  // open: gt, eq
  Comparator #(.width(64)) comparator_3 (.a(aluB), .b({64{1'b0}}), .lt(comparator_3_lt));  // open: gt, eq
  xor xor_2 (xor_2_out, comparator_2_lt, comparator_3_lt);
  Comparator #(.width(64)) comparator_4 (.a(subtractor_1_out), .b({64{1'b0}}), .lt(comparator_4_lt));  // open: gt, eq
  xnor xnor_1 (xnor_1_out, comparator_2_lt, comparator_4_lt);
  and and_2 (and_2_out, xnor_1_out, xor_2_out);
  Multiplexer #(.select(2)) multiplexer_2 (
    .in0(1'b0), .in1(1'b0), .in2(adder_1_cout), .in3(and_2_out), .out(Overflow), .sel(ALUfun));

  // Notes on the sheet:
  //   ALUfun: 00 = AND | 01 = NOR | 10 = + | 11 = -
  //   change overflow
endmodule

module condition (
  input  zeroflag,
  input  signflag,
  input  overflow,
  input  [3:0] ifun,
  output out_5
);

  wire and_1_out, not_1_out, not_2_out, not_3_out, not_4_out, or_1_out, xor_1_out, xor_2_out, xor_3_out,
       xor_4_out;

  xor xor_1 (xor_1_out, signflag, overflow);
  or or_1 (or_1_out, xor_1_out, zeroflag);
  xor xor_2 (xor_2_out, signflag, overflow);
  not not_1 (not_1_out, zeroflag);
  xor xor_3 (xor_3_out, signflag, overflow);
  not not_2 (not_2_out, xor_3_out);
  xor xor_4 (xor_4_out, signflag, overflow);
  not not_3 (not_3_out, xor_4_out);
  Multiplexer #(.select(3)) multiplexer_1 (
    .in0(1'b1), .in1(or_1_out), .in2(xor_2_out), .in3(zeroflag), .in4(not_1_out), .in5(not_2_out),
    .in6(and_1_out), .out(out_5), .sel(ifun[2:0]));  // open: in7
  not not_4 (not_4_out, zeroflag);
  and and_1 (and_1_out, not_3_out, not_4_out);
endmodule

module Memory (
  input  [3:0] icode,
  input  [63:0] valE,
  input  [63:0] valP,
  input  [63:0] valA,
  input  CLK,
  output [63:0] valM
);

  wire MAddr_out, MCntrl_out, not_1_out;
  wire [63:0] multiplexer_1_out;

  PLA #(.in_width(4), .out_width(1), .\table ("0100 0 # rmmovq - valE\n0101 0 # mrmovq - valE\n1010 0 # pushq - valE\n1011 1 # popq - valA")) MAddr (
    .in(icode), .out(MAddr_out));
  Multiplexer #(.width(64)) multiplexer_1 (.in0(valE), .in1(valA), .out(multiplexer_1_out), .sel(MAddr_out));
  PLA #(.in_width(4), .out_width(1), .\table ("0100 1 # rmmovq - write\n0101 0 # mrmovq - read\n1010 1 # pushq - write\n1011 0 # popq - read")) MCntrl (
    .in(icode), .out(MCntrl_out));
  not not_1 (not_1_out, MCntrl_out);
  DataMemory datamemory_1 (
    .address(multiplexer_1_out), .write(MCntrl_out), .read(not_1_out), .CLK(CLK), .data(valA), .data_out(valM));

  // Notes on the sheet:
  //   0 = read | 1 = write
endmodule

module DataMemory (
  input  [63:0] address,
  input  write,
  input  read,
  input  CLK,
  input  [63:0] data,
  output [63:0] data_out
);

  RAM #(.addrWidth(16), .dataWidth(64)) ram_1 (
    .addr(address[15:0]), .we(write), .oe(read), .clk(CLK), .din(data), .dout(data_out));
endmodule
